# Fritzing sketch car (saved by Fritzing 0.9.3b)

parts:
  Часть1 = Arduino Uno (Rev3)
  S1 = H-Bridge with L298N
  M1 = DC Motor
  M2 = DC Motor
  VCC1 = Battery block 9V

nets:
  GND: Часть1.GND, S1.GND, VCC1.-
  N1: Часть1.D2, S1.ENA
  N2: Часть1.D3_PWM, S1.IN1
  N3: Часть1.D4, S1.IN2
  N4: Часть1.D5_PWM, S1.IN3
  N5: Часть1.D6_PWM, S1.IN4
  N6: Часть1.D7, S1.ENB
  5V: Часть1.5V, S1.5V
  N7: S1.12V, VCC1.+
  N8: S1.M1-01, M2.pin_2
  N9: S1.M1-02, M2.pin_1
  N10: S1.M2-01, M1.pin_1
  N11: S1.M2-02, M1.pin_2

custom parts:
  H-Bridge with L298N: h-bridge

// code stored in the sketch: car.ino

/**


* @link https://github.com/Almadef/car/


* @copyright Copyright (c) 2019 Chuvashov Mikhail 


* @license https://github.com/Almadef/car/blob/master/LICENSE

*/
